# Fritzing sketch Untitled Sketch 3 (saved by Fritzing 0.9.3b)
breadboards: 1

parts:
  Part1 = Arduino Nano (Rev3.0)
  Part2 = Motor Driver 1A Dual TB6612FNG
  R1 = PHOTOCELL [package=photocell]
  M1 = Stepper Motor - Unipolar

nets:
  N1: Part1.GND, R1.P$2
  N2: Part1.D6, M1.B
  N3: Part1.D8, M1.C
  N4: Part1.A6, R1.P$1
  N5: Part1.A4, Part2.AIN2
  N6: Part1.A2, Part2.AIN1
  N7: Part2.A02, M1.D
  N8: Part2.A01, M1.A
  N9: Part2.GND, M1.COMMON_1
  N10: Part2.VCC, M1.COMMON_2

// code stored in the sketch: door fritzing.ino
void setup() {
  
pinMode(A2, OUTPUT);
pinMode(A4, OUTPUT);
pinMode(6, INPUT_PULLUP);
pinMode(8, INPUT_PULLUP);

}

void loop() {
  
Serial.begin(9600);
 unsigned int AnalogValue;
// int encoder1 = digitalRead(6);
 //int encoder2= digitalRead(8);
//Serial.println(encoder1);
//Serial.println(encoder2);
AnalogValue = analogRead(A6);
if(AnalogValue > 50) {
    digitalWrite(A2, HIGH);
  //  digitalWrite(A4, LOW);
    
}

if(!(AnalogValue > 50)) 
    digitalWrite(A2, LOW);
   // digitalWrite(A4, HIGH);

//Serial.println(AnalogValue);
}
